// Logisim project PC_4_bit.circ as structural Verilog: 4 circuits, main circuit main
module main (
  input  in_1,
  output [3:0] out_2
);

  wire and_1_out, clock_1_out, CONTROL_alusrc, CONTROL_branch, CONTROL_jump, CONTROL_memread,
       CONTROL_memtoreg, CONTROL_memwrite, CONTROL_regdst, CONTROL_regwrite, mips_alu_4_bit_1_p4;
  wire [2:0] Instruction_instr_3_5, Instruction_instr_6_8, Instruction_instr_9_11, multiplexer_1_out;
  wire [3:0] adder_1_out, adder_2_out, CONTROL_alucontrol, Instruction_iinstr_12_15, Instruction_instr_2_5,
       mips_alu_4_bit_1_p5, multiplexer_2_out, multiplexer_3_out, multiplexer_4_out, multiplexer_5_out,
       ram_1_data, registers_1_readdata1, registers_1_readdata2;
  wire [15:0] rom_1_data;

  Counter #(.width(4), .max('hf)) counter_1 (
    .load(1'b1), .D(multiplexer_5_out), .count(1'b0), .Q(out_2), .clk(clock_1_out), .clr(1'b0));  // open: carry
  ROM #(.addrWidth(4), .dataWidth(16)) rom_1 (.addr(out_2), .data(rom_1_data), .sel(in_1));
  Clock clock_1 (.out(clock_1_out));
  Adder #(.width(4)) adder_1 (.a(out_2), .b(4'b0001), .out(adder_1_out), .cin(1'b0));  // open: cout
  Instruction Instruction (
    .InstrMem(rom_1_data), .Instr_2_5(Instruction_instr_2_5), .Instr_3_5(Instruction_instr_3_5),
    .Instr_6_8(Instruction_instr_6_8), .Instr_9_11(Instruction_instr_9_11),
    .iinstr_12_15(Instruction_iinstr_12_15));
  Control CONTROL (
    .in_1(Instruction_iinstr_12_15), .RegDst(CONTROL_regdst), .ALUsrc(CONTROL_alusrc),
    .MemToReg(CONTROL_memtoreg), .RegWrite(CONTROL_regwrite), .MemRead(CONTROL_memread),
    .MemWrite(CONTROL_memwrite), .Branch(CONTROL_branch), .Jump(CONTROL_jump), .ALUControl(CONTROL_alucontrol));
  Multiplexer #(.width(3)) multiplexer_1 (
    .in0(Instruction_instr_9_11), .in1(Instruction_instr_3_5), .out(multiplexer_1_out), .sel(CONTROL_regdst));  // open: en
  Registers registers_1 (
    .WriteData(multiplexer_3_out), .WriteReg(multiplexer_1_out), .Regwrite(CONTROL_regwrite),
    .ReadReg1(Instruction_instr_9_11), .ReadReg2(Instruction_instr_6_8), .ReadData2(registers_1_readdata2),
    .CLK(clock_1_out), .ReadData1(registers_1_readdata1));
  Adder #(.width(4)) adder_2 (.a(adder_1_out), .b(Instruction_instr_2_5), .out(adder_2_out), .cin(1'b0));  // open: cout
  Multiplexer #(.width(4)) multiplexer_2 (
    .in0(registers_1_readdata2), .in1(Instruction_instr_2_5), .out(multiplexer_2_out), .sel(CONTROL_alusrc));  // open: en
  // MIPS_ALU_4_bit mips_alu_4_bit_1: pin names not known; wires that end beside it: registers_1_readdata1, multiplexer_2_out, CONTROL_alucontrol, mips_alu_4_bit_1_p4, mips_alu_4_bit_1_p5
  Multiplexer #(.width(4)) multiplexer_3 (
    .in0(mips_alu_4_bit_1_p5), .in1(ram_1_data), .out(multiplexer_3_out), .sel(CONTROL_memtoreg));  // open: en
  Multiplexer #(.width(4)) multiplexer_4 (
    .in0(adder_1_out), .in1(adder_2_out), .out(multiplexer_4_out), .sel(and_1_out));  // open: en
  and and_1 (and_1_out, CONTROL_branch, mips_alu_4_bit_1_p4);
  Multiplexer #(.width(4)) multiplexer_5 (
    .in0(multiplexer_4_out), .in1(rom_1_data[3:0]), .out(multiplexer_5_out), .sel(CONTROL_jump));  // open: en
  RAM #(.addrWidth(4), .dataWidth(4), .bus("separate")) ram_1 (
    .addr(mips_alu_4_bit_1_p5), .din(registers_1_readdata2), .data(ram_1_data), .str(CONTROL_memwrite),
    .clk(clock_1_out), .ld(CONTROL_memread));  // open: sel, clr

  // Notes on the sheet:
  //   contents of rom_1 (hex, n*v repeats v):
  //   5050 1208 2484 36c4 4720 ab28 91c4 7088 c284 6bc4 ba40 57d0 8021
endmodule

module Instruction (
  input  [15:0] InstrMem,
  output [3:0] Instr_2_5,
  output [2:0] Instr_3_5,
  output [2:0] Instr_6_8,
  output [2:0] Instr_9_11,
  output [3:0] iinstr_12_15
);


  assign iinstr_12_15 = InstrMem[15:12];
  assign Instr_2_5 = InstrMem[5:2];
  assign Instr_3_5 = InstrMem[5:3];
  assign Instr_6_8 = InstrMem[8:6];
  assign Instr_9_11 = InstrMem[11:9];
endmodule

module Control (
  input  [3:0] in_1,
  output RegDst,
  output ALUsrc,
  output MemToReg,
  output RegWrite,
  output MemRead,
  output MemWrite,
  output Branch,
  output Jump,
  output [3:0] ALUControl
);

  wire and_1_out, and_2_out, and_3_out, and_4_out, and_5_out, and_6_out, and_7_out, and_8_out, and_9_out,
       and_14_out, nor_1_out, nor_2_out, not_1_out, not_2_out, not_3_out, not_4_out, not_5_out, not_6_out,
       not_7_out, not_8_out, not_9_out, xnor_1_out;

  and and_1 (and_1_out, in_1[1], in_1[2], not_2_out);
  not not_1 (not_1_out, in_1[1]);
  and and_2 (and_2_out, in_1[1], in_1[0]);
  not not_2 (not_2_out, in_1[0]);
  not not_3 (not_3_out, in_1[2]);
  not not_4 (not_4_out, in_1[0]);
  not not_5 (not_5_out, in_1[3]);
  and and_3 (and_3_out, not_5_out, in_1[0]);
  not not_6 (not_6_out, in_1[0]);
  and and_4 (and_4_out, in_1[3], in_1[0]);
  not not_7 (not_7_out, in_1[2]);
  xnor xnor_1 (xnor_1_out, in_1[0], in_1[1]);
  nor nor_1 (nor_1_out, in_1[0], in_1[1]);
  and and_5 (and_5_out, not_5_out, in_1[1]);
  and and_6 (and_6_out, not_5_out, not_3_out, in_1[0]);
  nor nor_2 (nor_2_out, in_1[3], in_1[1]);
  and and_7 (and_7_out, in_1[1], in_1[3], not_6_out);
  not not_8 (not_8_out, in_1[2]);
  not not_9 (not_9_out, in_1[3]);
  or or_1 (RegWrite, not_7_out, xnor_1_out);
  or or_2 (ALUControl[1], and_3_out, and_5_out, and_2_out);
  or or_3 (ALUControl[2], and_6_out, and_1_out);
  or or_4 (RegDst, in_1[2], nor_2_out, and_7_out);
  and and_8 (and_8_out, in_1[3], in_1[2]);
  and and_9 (and_9_out, not_8_out, not_9_out, in_1[1]);
  and and_10 (MemRead, in_1[3], in_1[1], in_1[0]);
  and and_11 (MemWrite, not_1_out, in_1[2], in_1[0]);
  and and_12 (Branch, in_1[2], in_1[1], not_4_out);
  nor nor_3 (Jump, in_1[2], in_1[1], in_1[0]);
  and and_13 (ALUControl[0], nor_1_out, not_7_out, in_1[3]);
  and and_14 (and_14_out, in_1[0], not_1_out, in_1[2]);
  or or_5 (ALUsrc, and_4_out, and_8_out, and_14_out, and_9_out);

  assign ALUControl[3] = 1'b0;
  assign MemToReg = MemRead;
endmodule

module Registers (
  input  [3:0] WriteData,
  input  [2:0] WriteReg,
  input  Regwrite,
  input  [2:0] ReadReg1,
  input  [2:0] ReadReg2,
  input  CLK,
  output [3:0] ReadData1,
  output [3:0] ReadData2
);

  wire and_1_out, and_2_out, and_3_out, and_4_out, and_5_out, and_6_out, and_7_out, and_8_out, and_9_out,
       and_10_out, and_11_out, and_12_out, and_13_out, and_14_out, and_15_out, and_16_out, not_1_out,
       not_2_out, not_3_out;
  wire [3:0] register_1_q, register_2_q, register_3_q, register_4_q, register_5_q, register_6_q,
       register_7_q, register_8_q;

  not not_1 (not_1_out, WriteReg[2]);
  not not_2 (not_2_out, WriteReg[1]);
  not not_3 (not_3_out, WriteReg[0]);
  and and_1 (and_1_out, not_3_out, not_2_out, not_1_out);
  and and_2 (and_2_out, not_2_out, not_1_out, WriteReg[0]);
  and and_3 (and_3_out, not_3_out, WriteReg[1], not_1_out);
  and and_4 (and_4_out, not_1_out, WriteReg[1], WriteReg[0]);
  and and_5 (and_5_out, WriteReg[2], not_2_out, not_3_out);
  and and_6 (and_6_out, WriteReg[2], not_2_out, WriteReg[0]);
  and and_7 (and_7_out, WriteReg[2], WriteReg[1], not_3_out);
  and and_8 (and_8_out, WriteReg[2], WriteReg[1], WriteReg[0]);
  and and_9 (and_9_out, Regwrite, and_1_out);
  and and_10 (and_10_out, Regwrite, and_2_out);
  and and_11 (and_11_out, Regwrite, and_3_out);
  and and_12 (and_12_out, and_4_out, Regwrite);
  and and_13 (and_13_out, and_5_out, Regwrite);
  and and_14 (and_14_out, and_6_out, Regwrite);
  and and_15 (and_15_out, and_7_out, Regwrite);
  and and_16 (and_16_out, and_8_out, Regwrite);
  Register #(.width(4)) register_1 (.D(WriteData), .en(and_9_out), .Q(register_1_q), .clk(CLK), .clr(1'b0));
  Register #(.width(4)) register_2 (.D(WriteData), .en(and_10_out), .Q(register_2_q), .clk(CLK), .clr(1'b0));
  Register #(.width(4)) register_3 (.D(WriteData), .en(and_11_out), .Q(register_3_q), .clk(CLK), .clr(1'b0));
  Register #(.width(4)) register_4 (.D(WriteData), .en(and_12_out), .Q(register_4_q), .clk(CLK), .clr(1'b0));
  Register #(.width(4)) register_5 (.D(WriteData), .en(and_13_out), .Q(register_5_q), .clk(CLK), .clr(1'b0));
  Register #(.width(4)) register_6 (.D(WriteData), .en(and_14_out), .Q(register_6_q), .clk(CLK), .clr(1'b0));
  Register #(.width(4)) register_7 (.D(WriteData), .en(and_15_out), .Q(register_7_q), .clk(CLK), .clr(1'b0));
  Register #(.width(4)) register_8 (.D(WriteData), .en(and_16_out), .Q(register_8_q), .clk(CLK), .clr(1'b0));
  Multiplexer #(.select(3), .width(4)) multiplexer_1 (
    .in0(register_1_q), .in1(register_2_q), .in2(register_3_q), .in3(register_4_q), .in4(register_5_q),
    .in5(register_6_q), .in6(register_7_q), .in7(register_8_q), .out(ReadData1), .sel(ReadReg1));  // open: en
  Multiplexer #(.select(3), .width(4)) multiplexer_2 (
    .in0(register_1_q), .in1(register_2_q), .in2(register_3_q), .in3(register_4_q), .in4(register_5_q),
    .in5(register_6_q), .in6(register_7_q), .in7(register_8_q), .out(ReadData2), .sel(ReadReg2));  // open: en
endmodule
